// Logisim project Guess_The_Number_Xtreme.circ as structural Verilog: 10 circuits, main circuit main
// x
module main (
  input  SX,
  input  in_2,
  input  in_3,
  input  [3:0] OB,
  input  in_5,
  input  in_6,
  input  in_7,
  input  in_8
);

  wire A_VENCEU, B_JOGANDO, B_VENCEU, CHUTANDO_X, CHUTANDO_Y, chutar, CONFIGURAR, coordenadas_1_p2,
       coordenadas_1_p3, coordenadas_1_p5, coordenadas_1_p6, coordenadas_1_p7, coordenadas_1_p8,
       coordenadas_1_p9, coordenadas_1_p10, coordenadas_1_p11, coordenadas_1_p12, coordenadas_1_p13,
       coordenadas_1_p14, coordenadas_1_p16, coordenadas_1_p17, coordenadas_1_p18, coordenadas_1_p19,
       coordenadas_1_p20, coordenadas_1_p21, decrementar_min_sec_1_p4, decrementar_min_sec_1_p6, dma_t,
       dsa_t, EMPATE, FIM_DE_JOGO, IGUAL, MAIOR, MENOR, proximo, RESET, SA, SB, START, SX_t, SY, tunnel,
       uma_t, undriven, undriven_3, undriven_5, usa_t;
  wire [3:0] ACERTOU, DMA, GA, GB, OA, PB, UMA, undriven_2, undriven_4, USA, XH, YH;

  Button button_1 (.out(dma_t));
  Button button_2 (.out(OA[0]));
  Hex_Digit_Display hex_digit_display_1 (.value(DMA));  // open: dp
  Hex_Digit_Display hex_digit_display_2 (.value(UMA));  // open: dp
  LED led_1 (.in(SA));
  Hex_Digit_Display hex_digit_display_3 (.value(ACERTOU));  // open: dp
  Button button_3 (.out(dsa_t));
  LED A3 ();  // open: in
  LED #(.active("false")) led_2 ();  // open: in
  Hex_Digit_Display hex_digit_display_4 ();  // open: value, dp
  LED led_3 (.in(undriven));
  Button button_4 (.out(usa_t));
  Hex_Digit_Display hex_digit_display_5 (.value(USA));  // open: dp
  LED led_4 (.in(SX_t));
  LED led_5 (.in(A_VENCEU));
  Button button_5 (.out(START));
  LED u_usa (.in(MAIOR));
  Button u_B_JOGANDO (.out(proximo));
  Hex_Digit_Display hex_digit_display_6 (.value(XH));  // open: dp
  LED led_6 (.in(CHUTANDO_X));
  LED led_7 (.in(FIM_DE_JOGO));
  LED led_8 (.in(EMPATE));
  LED led_9 (.in(tunnel));
  Button button_6 (.out(CONFIGURAR));
  LED led_10 (.in(ACERTOU[0]));
  LED led_11 (.in(ACERTOU[0]));
  LED led_12 (.in(IGUAL));
  Button button_7 (.out(chutar));
  LED led_13 (.in(SY));
  Hex_Digit_Display hex_digit_display_7 (.value(YH));  // open: dp
  LED led_14 (.in(CHUTANDO_Y));
  LED led_15 (.in(B_VENCEU));
  Button button_8 (.out(RESET));
  Button button_9 (.out(RESET));
  LED led_16 (.in(MENOR));
  Hex_Digit_Display #(.active("false")) hex_digit_display_8 (.value(PB));  // open: dp
  LED #(.active("false")) led_17 ();  // open: in
  LED #(.active("false")) led_18 ();  // open: in
  Hex_Digit_Display hex_digit_display_9 (.value(undriven_2), .dp(undriven_3));
  Hex_Digit_Display hex_digit_display_10 (.value(undriven_2), .dp(undriven_3));
  LED led_19 (.in(SB));
  Hex_Digit_Display hex_digit_display_11 (.value(GB));  // open: dp
  LED led_20 (.in(B_JOGANDO));
  Hex_Digit_Display hex_digit_display_12 (.value(undriven_4), .dp(undriven_5));
  Hex_Digit_Display hex_digit_display_13 (.value(undriven_4), .dp(undriven_5));
  Hex_Digit_Display hex_digit_display_14 ();  // open: value, dp
  // Coordenadas coordenadas_1: pin names not known; wires that end beside it: OA, coordenadas_1_p2, coordenadas_1_p3, proximo, coordenadas_1_p5, coordenadas_1_p6, coordenadas_1_p7, coordenadas_1_p8, coordenadas_1_p9, coordenadas_1_p10, coordenadas_1_p11, coordenadas_1_p12, coordenadas_1_p13, coordenadas_1_p14, SX_t, coordenadas_1_p16, coordenadas_1_p17, coordenadas_1_p18, coordenadas_1_p19, coordenadas_1_p20, coordenadas_1_p21, ACERTOU, PB, ACERTOU, MAIOR, IGUAL, MENOR, dma_t
  // Coordenadas coordenadas_2: pin names not known; wires that end beside it: CHUTANDO_X, coordenadas_1_p2, coordenadas_1_p14, coordenadas_1_p6, coordenadas_1_p10, coordenadas_1_p12, coordenadas_1_p17, coordenadas_1_p19, coordenadas_1_p21, PB, coordenadas_1_p17
  // numero_negativo Jogador_A: pin names not known; wires that end beside it: SX, in_2, in_3, OB, OA, SA, GA
  // decrementar_min_sec decrementar_min_sec_1: pin names not known; wires that end beside it: uma_t, dsa_t, usa_t, decrementar_min_sec_1_p4, decrementar_min_sec_1_p4, decrementar_min_sec_1_p6, decrementar_min_sec_1_p6
  Clock clock_1 (.out(decrementar_min_sec_1_p4));
  // Pins of 1 and 4 bits meet at OB
  // Pins of 1 and 4 bits meet at OA
  // Pins of 1 and 4 bits meet at ACERTOU

  // Other names for the same wires on the sheet: A0[3:0] = OB; A1 = in_3; A2 = in_2; A3 = SX; B0 = in_8; B1 = in_7;
  //   B2 = in_6; B3 = in_5; PA[3:0] = ACERTOU
endmodule

module Flip_Flop_SR (
  input  S_R,
  input  Preset,
  input  Enable,
  input  Clear,
  input  Clear_2,
  output out_6
);

  wire not_1_out, s_r_ff_1_qn, undriven;

  not not_1 (not_1_out, S_R);
  not not_2 (not_1_out, S_R);
  S_R_Flip_Flop s_r_ff_1 (
    .S(S_R), .clk(undriven), .R(not_1_out), .Q(out_6), .Qn(s_r_ff_1_qn), .preset(Preset), .reset(Clear),
    .en(Enable));
  S_R_Flip_Flop s_r_ff_2 (
    .S(S_R), .clk(undriven), .R(not_1_out), .Q(out_6), .Qn(s_r_ff_1_qn), .preset(Preset), .reset(Clear),
    .en(Enable));

  assign Clear_2 = Clear;
endmodule

module Decrementador (
  input  Clock,
  input  Clock_2,
  input  Enable,
  input  Clear,
  input  [3:0] in_5,
  input  [3:0] valor_retorno,
  output [3:0] out_7
);

  wire comparator_1_eq, comparator_1_gt, comparator_1_lt, undriven;
  wire [3:0] adder_1_out, multiplexer_1_out;

  Hex_Digit_Display hex_digit_display_1 (.value(out_7));  // open: dp
  Flip_Flop_SR flip_flop_sr_1 (
    .S_R(multiplexer_1_out[3]), .Preset(Clock), .Enable(undriven), .Clear(Enable), .Clear_2(Clear),
    .out_6(out_7[3]));
  Flip_Flop_SR flip_flop_sr_2 (
    .S_R(multiplexer_1_out[2]), .Preset(Clock), .Enable(undriven), .Clear(Enable), .Clear_2(Clear),
    .out_6(out_7[2]));
  Flip_Flop_SR flip_flop_sr_3 (
    .S_R(multiplexer_1_out[1]), .Preset(Clock), .Enable(undriven), .Clear(Enable), .Clear_2(Clear),
    .out_6(out_7[1]));
  Multiplexer #(.width(4)) multiplexer_1 (
    .in0(adder_1_out), .in1(in_5), .out(multiplexer_1_out), .sel(comparator_1_eq));  // open: en
  Flip_Flop_SR flip_flop_sr_4 (
    .S_R(multiplexer_1_out[0]), .Preset(Clock), .Enable(undriven), .Clear(Enable), .Clear_2(Clear),
    .out_6(out_7[0]));
  Hex_Digit_Display hex_digit_display_2 (.value(adder_1_out));  // open: dp
  Adder #(.width(4)) adder_1 (.a(out_7), .b(4'b1111), .out(adder_1_out));  // open: cin, cout
  Comparator #(.width(4), .value('hf)) comparator_1 (
    .a(adder_1_out), .b(4'b1111), .gt(comparator_1_gt), .eq(comparator_1_eq), .lt(comparator_1_lt));
  Comparator #(.width(4)) comparator_2 (
    .a(adder_1_out), .b(4'b1111), .gt(comparator_1_gt), .eq(comparator_1_eq), .lt(comparator_1_lt));

  assign Clock_2 = Clock;
  assign valor_retorno = in_5;
endmodule

module Verificador_9 (
  input  Enable
);

  wire and_1_out, comparator_1_eq, comparator_2_eq, comparator_3_eq, comparator_4_eq, comparator_4_gt,
       comparator_4_lt, not_1_out, undriven, undriven_2, undriven_3, undriven_4, undriven_6;
  wire [3:0] and_2_out, decrementador_1_out_7, decrementador_2_out_7, decrementador_3_out_7,
       decrementador_6_out_7, undriven_5;

  and and_1 (and_1_out, Enable, not_1_out);
  not not_1 (not_1_out, comparator_2_eq);
  Hex_Digit_Display hex_digit_display_1 (.value(decrementador_1_out_7));  // open: dp
  Decrementador decrementador_1 (
    .Clock(comparator_1_eq), .Enable(and_1_out), .in_5(4'b0001), .out_7(decrementador_1_out_7));  // open: Clock_2, Clear, valor_retorno
  Hex_Digit_Display hex_digit_display_2 (.value(decrementador_2_out_7), .dp(undriven));
  Hex_Digit_Display hex_digit_display_3 (.value(decrementador_2_out_7), .dp(undriven));
  Decrementador decrementador_2 (
    .Clock(comparator_3_eq), .Enable(and_1_out), .in_5(4'b1111), .out_7(decrementador_2_out_7));  // open: Clock_2, Clear, valor_retorno
  Comparator #(.width(4)) comparator_1 (.a(decrementador_2_out_7), .b(4'b1111), .eq(comparator_1_eq));  // open: gt, lt
  assign and_2_out = ~decrementador_1_out_7 & ~decrementador_2_out_7 & ~decrementador_3_out_7 & ~decrementador_6_out_7;  // AND_Gate and_2, 4 bits wide
  Hex_Digit_Display hex_digit_display_4 (.value(decrementador_3_out_7), .dp(undriven_3));
  Hex_Digit_Display hex_digit_display_5 (.value(decrementador_3_out_7), .dp(undriven_3));
  Decrementador decrementador_3 (
    .Clock(comparator_4_eq), .Clock_2(undriven_2), .Enable(and_1_out), .Clear(undriven_4), .in_5(4'b0001),
    .valor_retorno(undriven_5), .out_7(decrementador_3_out_7));
  Decrementador decrementador_4 (
    .Clock(comparator_4_eq), .Clock_2(undriven_2), .Enable(and_1_out), .Clear(undriven_4), .in_5(4'b0001),
    .valor_retorno(undriven_5), .out_7(decrementador_3_out_7));
  Decrementador decrementador_5 (
    .Clock(comparator_4_eq), .Clock_2(undriven_2), .Enable(and_1_out), .Clear(undriven_4), .in_5(4'b0001),
    .valor_retorno(undriven_5), .out_7(decrementador_3_out_7));
  Comparator #(.width(4)) comparator_2 (.a(and_2_out), .b(4'b1111), .eq(comparator_2_eq));  // open: gt, lt
  Comparator #(.width(4)) comparator_3 (.a(decrementador_3_out_7), .b(4'b0001), .eq(comparator_3_eq));  // open: gt, lt
  Hex_Digit_Display hex_digit_display_6 (.value(decrementador_6_out_7));  // open: dp
  Decrementador decrementador_6 (
    .Clock(undriven_6), .Enable(and_1_out), .in_5(4'b1111), .out_7(decrementador_6_out_7));  // open: Clock_2, Clear, valor_retorno
  Comparator #(.width(4)) comparator_4 (
    .a(decrementador_6_out_7), .b(4'b1111), .gt(comparator_4_gt), .eq(comparator_4_eq), .lt(comparator_4_lt));
  Comparator #(.width(4)) comparator_5 (
    .a(decrementador_6_out_7), .b(4'b1111), .gt(comparator_4_gt), .eq(comparator_4_eq), .lt(comparator_4_lt));
endmodule

module decrementar_min_sec (
  input  Clear,
  input  Enable,
  input  DSA,
  input  uma,
  input  uma_2,
  input  uda,
  input  CLOCK,
  output [3:0] DMA,
  output [3:0] UMA_3,
  output [3:0] out_10,
  output [3:0] USA
);

  wire and_2_out, comparator_1_eq, comparator_1_gt, comparator_1_lt, comparator_3_eq, comparator_4_eq,
       comparator_5_eq, multiplexer_1_out, multiplexer_2_out, multiplexer_3_out, not_1_out, not_2_out,
       or_1_out, or_2_out, or_3_out, or_4_out, undriven, undriven_2;
  wire [3:0] and_1_p3, and_1_p6;

  not not_1 (not_1_out, DSA);
  Hex_Digit_Display hex_digit_display_1 (.value(DMA));  // open: dp
  Decrementador decrementador_1 (
    .Clock(multiplexer_1_out), .Enable(or_1_out), .Clear(Clear), .in_5(4'b0101), .out_7(DMA));  // open: Clock_2, valor_retorno
  or or_1 (or_1_out, DSA, not_1_out);
  Multiplexer multiplexer_1 (.in0(uda), .in1(comparator_1_eq), .out(multiplexer_1_out), .sel(DSA));  // open: en
  Hex_Digit_Display hex_digit_display_2 (.value(UMA_3));  // open: dp
  Decrementador decrementador_2 (
    .Clock(undriven), .Enable(or_2_out), .Clear(Clear), .in_5(4'b1001), .out_7(UMA_3));  // open: Clock_2, valor_retorno
  or or_2 (or_2_out, DSA, not_1_out);
  Comparator #(.width(4)) comparator_1 (
    .a(UMA_3), .b(4'b1001), .gt(comparator_1_gt), .eq(comparator_1_eq), .lt(comparator_1_lt));
  Comparator #(.width(4)) comparator_2 (
    .a(UMA_3), .b(4'b1001), .gt(comparator_1_gt), .eq(comparator_1_eq), .lt(comparator_1_lt));
  // AND_Gate #(.width(4)) and_1: pin names not known; wires that end beside it: DMA, UMA_3, and_1_p3, out_10, USA, and_1_p6
  Hex_Digit_Display hex_digit_display_3 (.value(out_10));  // open: dp
  Decrementador decrementador_3 (
    .Clock(multiplexer_2_out), .Enable(or_3_out), .Clear(Clear), .in_5(4'b0101), .out_7(out_10));  // open: Clock_2, valor_retorno
  or or_3 (or_3_out, DSA, not_1_out);
  Multiplexer multiplexer_2 (.in0(uma_2), .in1(comparator_5_eq), .out(multiplexer_2_out), .sel(DSA));  // open: en
  Comparator #(.width(4)) comparator_3 (.a(out_10), .b(4'b0101), .eq(comparator_3_eq));  // open: gt, lt
  Comparator #(.width(4)) comparator_4 (.a(and_1_p3), .b(and_1_p6), .eq(comparator_4_eq));  // open: gt, lt
  Hex_Digit_Display hex_digit_display_4 (.value(USA));  // open: dp
  or or_4 (or_4_out, DSA, not_1_out);
  Multiplexer multiplexer_3 (.in0(undriven_2), .in1(and_2_out), .out(multiplexer_3_out), .sel(DSA));  // open: en
  Comparator #(.width(4)) comparator_5 (.a(USA), .b(4'b1001), .eq(comparator_5_eq));  // open: gt, lt
  and and_2 (and_2_out, not_2_out, CLOCK);
  Clock clock_1 (.out(CLOCK));
  Clock clock_2 (.out(CLOCK));
  not not_2 (not_2_out, comparator_4_eq);
  not not_3 (not_2_out, comparator_4_eq);

  assign Enable = DSA;
endmodule

module Entrada (
  input  A1,
  input  A0,
  output [3:0] resultado
);

  Hex_Digit_Display hex_digit_display_1 (.value({resultado[3:2], A1, A0}));  // open: dp

  assign resultado[1:0] = {A1, A0};
endmodule

// coordenadas
module Coordenadas (
  input  [3:0] a,
  input  [3:0] b,
  input  [3:0] b_2,
  input  proximo,
  input  in_5,
  input  chutar,
  output [3:0] PlacarA,
  output [3:0] PlacarA_2,
  output [3:0] PlacarA_3,
  output Jogador_A,
  output Acertou,
  output MAIOR,
  output MENOR,
  output MENOR_2,
  output SX,
  output SY,
  output Chutando_X,
  output MAIOR_2,
  output SX_2
);

  wire and_1_out, and_3_out, and_4_out, and_5_out, and_6_out, and_7_out, comparator_1_eq, comparator_2_eq,
       comparator_3_eq, comparator_4_eq, comparator_5_eq, comparator_7_eq, comparator_8_eq, comparator_8_gt,
       comparator_8_lt, comparator_9_eq, comparator_10_eq, comparator_10_gt, comparator_10_lt,
       numero_negativo_2_p1, or_1_out, undriven, undriven_2, undriven_3, undriven_4, undriven_5;
  wire [3:0] a_out, adder_1_out, adder_2_out, flip_flop_condicao_2_valor_saida,
       flip_flop_condicao_3_valor_saida, flip_flop_condicao_6_valor_saida, multiplexer_2_out, random_1_out,
       random_2_out, register_1_q, register_2_q;

  flip_flop_condicao flip_flop_condicao_1 ();  // open: Clock, Preset, Enable, Clear, valor_retorno, valor_max__1, valor_saida
  Hex_Digit_Display hex_digit_display_1 (.value(flip_flop_condicao_2_valor_saida));  // open: dp
  flip_flop_condicao flip_flop_condicao_2 (
    .Clock(proximo), .Preset(1'b0), .Enable(1'b1), .Clear(1'b0), .valor_retorno(4'b0000),
    .valor_max__1(4'b0011), .valor_saida(flip_flop_condicao_2_valor_saida));
  Comparator #(.width(4)) comparator_1 (
    .a(flip_flop_condicao_2_valor_saida), .b(4'b0010), .eq(comparator_1_eq));  // open: gt, lt
  Comparator #(.width(4)) comparator_2 (
    .a(flip_flop_condicao_2_valor_saida), .b(4'b0000), .eq(comparator_2_eq));  // open: gt, lt
  flip_flop_condicao flip_flop_condicao_3 (
    .Clock(comparator_2_eq), .Preset(undriven), .Enable(1'b1), .Clear(1'b0), .valor_retorno(4'b0000),
    .valor_max__1(4'b0010), .valor_saida(flip_flop_condicao_3_valor_saida));
  flip_flop_condicao flip_flop_condicao_4 (
    .Clock(comparator_2_eq), .Preset(undriven), .Enable(1'b1), .Clear(1'b0), .valor_retorno(4'b0000),
    .valor_max__1(4'b0010), .valor_saida(flip_flop_condicao_3_valor_saida));
  Comparator #(.width(4)) comparator_3 (
    .a(flip_flop_condicao_3_valor_saida), .b(4'b0000), .eq(comparator_3_eq));  // open: gt, lt
  not not_1 (Jogador_A, comparator_3_eq);
  Comparator #(.width(4)) comparator_4 (
    .a(flip_flop_condicao_2_valor_saida), .b(4'b0000), .eq(comparator_4_eq));  // open: gt, lt
  Comparator #(.width(4)) comparator_5 (
    .a(flip_flop_condicao_2_valor_saida), .b(4'b0001), .eq(comparator_5_eq));  // open: gt, lt
  Comparator #(.width(4)) comparator_6 (
    .a(flip_flop_condicao_2_valor_saida), .b(4'b0000), .eq(Chutando_X));  // open: gt, lt
  Multiplexer #(.width(4), .tristate("false")) u_a (
    .in0(a), .in1(b), .out(a_out), .sel(comparator_3_eq), .en(undriven_2));
  Multiplexer #(.width(4)) multiplexer_1 (.in0(a), .in1(b), .out(a_out), .sel(comparator_3_eq), .en(undriven_2));
  and and_1 (and_1_out, comparator_4_eq, chutar);
  and and_2 (and_1_out, comparator_4_eq, chutar);
  Hex_Digit_Display hex_digit_display_2 (.value(register_1_q));  // open: dp
  LED u_Chutando_X (.in(Chutando_X));
  LED Chutando_X_2 (.in(Chutando_X));
  Multiplexer #(.width(4), .value('h0)) multiplexer_2 (
    .in0(a), .in1(b), .out(multiplexer_2_out), .sel(comparator_3_eq));  // open: en
  Register #(.width(4)) register_1 (.D(a_out), .Q(register_1_q), .clk(and_1_out));  // open: en, clr
  and and_3 (and_3_out, chutar, comparator_5_eq);
  Comparator #(.width(4)) comparator_7 (
    .a(flip_flop_condicao_2_valor_saida), .b(4'b0001), .eq(comparator_7_eq));  // open: gt, lt
  Register #(.width(4)) register_2 (.D(multiplexer_2_out), .Q(register_2_q), .clk(and_3_out));  // open: en, clr
  Hex_Digit_Display hex_digit_display_3 (.value(register_2_q));  // open: dp
  LED Chutando_Y (.in(comparator_7_eq));
  and and_4 (and_4_out, comparator_2_eq, Acertou);
  Adder #(.width(4)) adder_1 (.a(register_1_q), .b(register_2_q), .out(adder_1_out));  // open: cin, cout
  // numero_negativo numero_negativo_1: pin names not known; wires that end beside it: MAIOR_2, SX, register_1_q[0], register_1_q[1], register_1_q[2]
  Hex_Digit_Display hex_digit_display_4 (.value(random_1_out));  // open: dp
  Random #(.width(4)) random_1 (.clk(and_4_out), .out(random_1_out));  // open: next, clr
  Random #(.width(4)) random_2 (.clk(and_4_out), .out(random_2_out));  // open: next, clr
  Hex_Digit_Display hex_digit_display_5 (.value(random_2_out));  // open: dp
  // numero_negativo numero_negativo_2: pin names not known; wires that end beside it: numero_negativo_2_p1, SX_2, SY, register_2_q[0], register_2_q[1], register_2_q[2]
  // numero_negativo numero_negativo_3: pin names not known; wires that end beside it: numero_negativo_2_p1, SX_2, SY, register_2_q[0], register_2_q[1], register_2_q[2]
  Adder #(.width(4)) adder_2 (.a(random_1_out), .b(random_2_out), .out(adder_2_out));  // open: cin, cout
  and and_5 (and_5_out, Jogador_A, Acertou);
  and and_6 (and_6_out, comparator_3_eq, Acertou);
  Comparator #(.width(4)) comparator_8 (
    .a(adder_1_out), .b(adder_2_out), .gt(comparator_8_gt), .eq(comparator_8_eq), .lt(comparator_8_lt));
  flip_flop_condicao flip_flop_condicao_5 (
    .Clock(and_5_out), .Preset(1'b0), .Enable(1'b1), .Clear(1'b0), .valor_retorno(4'b0000),
    .valor_max__1(4'b1111), .valor_saida(PlacarA));
  flip_flop_condicao flip_flop_condicao_6 (
    .Clock(and_6_out), .Preset(1'b0), .Enable(1'b1), .Clear(1'b0), .valor_retorno(4'b0000),
    .valor_max__1(4'b1111), .valor_saida(flip_flop_condicao_6_valor_saida));
  Comparator #(.width(4), .value('h0)) comparator_9 (
    .a(register_1_q), .b(random_1_out), .eq(comparator_9_eq));  // open: gt, lt
  Comparator #(.width(4), .value('hf)) comparator_10 (
    .a(register_2_q), .b(random_2_out), .gt(comparator_10_gt), .eq(comparator_10_eq), .lt(comparator_10_lt));
  Comparator #(.width(4)) comparator_11 (
    .a(register_2_q), .b(random_2_out), .gt(comparator_10_gt), .eq(comparator_10_eq), .lt(comparator_10_lt));
  Hex_Digit_Display hex_digit_display_6 (.value(PlacarA), .dp(undriven_3));
  Hex_Digit_Display hex_digit_display_7 (.value(PlacarA), .dp(undriven_3));
  Hex_Digit_Display hex_digit_display_8 (.value(flip_flop_condicao_6_valor_saida));  // open: dp
  and and_7 (and_7_out, comparator_9_eq, comparator_10_eq);
  LED A___B (.in(MAIOR));
  and and_8 (in_5, comparator_1_eq, comparator_8_eq);
  LED A____B (.in(in_5));
  and and_9 (MENOR, comparator_1_eq, comparator_8_lt);
  LED A___B_2 (.in(MENOR));
  and and_10 (Acertou, and_7_out, in_5);
  or or_1 (or_1_out, undriven_5, undriven_4);

  assign b_2 = b;
  assign MENOR_2 = MENOR;
  assign PlacarA_2 = PlacarA;
  assign PlacarA_3 = PlacarA;
endmodule

module flip_flop_condicao (
  input  Clock,
  input  Preset,
  input  Enable,
  input  Clear,
  input  [3:0] valor_retorno,
  input  [3:0] valor_max__1,
  output [3:0] valor_saida
);

  wire comparator_1_eq, undriven, undriven_2;
  wire [1:0] undriven_3;
  wire [3:0] adder_1_out;

  Hex_Digit_Display hex_digit_display_1 (.value(valor_saida));  // open: dp
  Flip_Flop_SR flip_flop_sr_1 (
    .S_R(undriven), .Preset(Clock), .Enable(Preset), .Clear(Enable), .Clear_2(Clear), .out_6(valor_saida[3]));
  Flip_Flop_SR flip_flop_sr_2 (
    .S_R(undriven_2), .Preset(Clock), .Enable(Preset), .Clear(Enable), .Clear_2(Clear), .out_6(valor_saida[2]));
  Flip_Flop_SR flip_flop_sr_3 (
    .S_R(undriven_3[1]), .Preset(Clock), .Enable(Preset), .Clear(Enable), .Clear_2(Clear),
    .out_6(valor_saida[1]));
  Flip_Flop_SR flip_flop_sr_4 (
    .S_R(undriven_3[0]), .Preset(Clock), .Enable(Preset), .Clear(Enable), .Clear_2(Clear),
    .out_6(valor_saida[0]));
  Hex_Digit_Display hex_digit_display_2 (.value(adder_1_out));  // open: dp
  Adder #(.width(4)) adder_1 (.a(valor_saida), .b(4'b0001), .out(adder_1_out));  // open: cin, cout
  Comparator #(.width(4)) comparator_1 (.a(adder_1_out), .b(valor_max__1), .eq(comparator_1_eq));  // open: gt, lt
endmodule

module numero_negativo (
  input  Entrada_3,
  input  Entrada_1,
  input  Entrada_0,
  output [3:0] \Saída ,
  output [3:0] \Saída_2 
);

  wire [3:0] not_1_out, undriven;

  Multiplexer #(.width(4)) multiplexer_1 (
    .in0({Entrada_1, Entrada_0, Entrada_1, Entrada_0}), .in1(undriven), .out(\Saída ), .sel(Entrada_1));  // open: en
  assign not_1_out = ~{Entrada_1, Entrada_0, Entrada_1, Entrada_0};  // NOT_Gate not_1, 4 bits wide
  // Pins of 2 and 4 bits meet at {Entrada_1, Entrada_0, Entrada_1, Entrada_0}

  assign Entrada_3 = Entrada_1;
  assign \Saída_2  = \Saída ;
endmodule

module cronometro (
  input  Clear,
  input  usa,
  output [3:0] \Saída ,
  output [3:0] original
);

  wire and_1_out, multiplexer_1_out, undriven, undriven_2, undriven_3, undriven_4, undriven_5, undriven_7,
       undriven_8;
  wire [3:0] decrementador_1_out_7, undriven_6;

  Decrementador decrementador_1 (
    .Clock(multiplexer_1_out), .Enable(undriven_3), .Clear(undriven_5), .in_5(undriven_6),
    .out_7(decrementador_1_out_7));  // open: Clock_2, valor_retorno
  Multiplexer multiplexer_1 (.in0(undriven_2), .in1(undriven_4), .out(multiplexer_1_out), .sel(undriven));  // open: en
  Hex_Digit_Display hex_digit_display_1 ();  // open: value, dp
  // NOT_Gate not_1 is placed but not wired
  and and_1 (and_1_out, undriven_7, undriven_8);
endmodule
